# Fritzing sketch tphMonitorSketch-RasPiZ (saved by Fritzing 0.9.3b)
breadboards: 1

parts:
  Raspberry_Pi_Zero1 = Raspberry Pi Zero
  Part1 = Adafruit Si7021 Temp Humidity [part_number="Adafruit #3251"]
  Part2 = Adafruit_BMP280
  Part3 = Adafruit DS1307 RTC Breakout [part_number="Adafruit #264"]
  Part4 = Micro Lipo Charger

nets:
  VIN: Raspberry_Pi_Zero1.3v3, Part1.VIN, Part2.VIN, Part3.VCC
  N1: Raspberry_Pi_Zero1.GPIO2, Part1.SDA, Part2.SDI/SDA, Part3.SDA
  N2: Raspberry_Pi_Zero1.GPIO3, Part1.SCL, Part2.SCK/SCL, Part3.SCL
  GND: Raspberry_Pi_Zero1.GND, Part1.GND, Part2.GND, Part3.GND, Part4.GND
  5V: Raspberry_Pi_Zero1.5V, Part4.5V

custom parts:
  Adafruit Si7021 Temp Humidity: It's summer and you're sweating and your hair's all frizzy and all you really want to know is why the weatherman said this morning that today's relative humidity would max out at a perfectly reasonable 42% when it feels more like 77%. Enter the Si7021 Temperature + Humidity Sensor - the best way to prove the weatherman wrong! This lovely sensor for Silicon labs has ± 3% relative humidity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
  Adafruit_BMP280: Bosch has stepped up their game with their new BMP280 sensor, an environmental sensor with temperature, barometric pressure that is the next generation upgrade to the BMP085/BMP180/BMP183. This sensor is great for all sorts of weather sensing and can even be used in both I2C and SPI! This precision sensor from Bosch is the best low-cost, precision sensing solution for measuring barometric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
  Adafruit DS1307 RTC Breakout: This is a great battery-backed real time clock (RTC) that allows your microcontroller project to keep track of time even if it is reprogrammed, or if the power is lost. Perfect for datalogging, clock-building, time stamping, timers and alarms, etc. The DS1307 is the most popular RTC - but it requires 5V power to work (although we've used it with 5V power and 3.3V logic successfully) PCB &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
  Micro Lipo Charger: Oh so handy, this little lipo charger is so small and easy to use you can keep it on your desk or mount it easily into any project! Simply plug it via any MicroUSB cable into a USB port and a 3.7V/4.2V lithium polymer or lithium ion rechargeable battery into the JST plug on the other end. There are two LEDs - one red and one green. While charging, the red LED is lit. When the battery is fully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
